// Logisim project myCPU.circ as structural Verilog: 23 circuits, main circuit main
module main (
  input  [7:0] in_1,
  input  [7:0] in_2,
  input  [3:0] in_3,
  input  [7:0] in_4,
  input  [7:0] in_5,
  input  [3:0] in_6,
  input  [7:0] in_7,
  input  [7:0] in_8,
  input  [3:0] in_9,
  output [7:0] out_10,
  output [7:0] out_11,
  output out_12,
  output [7:0] out_13,
  output out_14
);

  my8bitLU my8bitlu_1 (.A(in_1), .B(in_2), .in_3(in_3), .out_4(out_10));
  my8bitAU my8bitau_1 (.A(in_4), .B(in_5), .S2(in_6[2]), .S1(in_6[1]), .S0(in_6[0]), .out_6(out_11), .Cout(out_12));
  my8bitALU my8bitalu_1 (.A(in_7), .B(in_8), .in_3(in_9), .out_4(out_13), .Carry(out_14));
endmodule

module myNOT (
  input  in_1,
  output out_2
);

  nand nand_1 (out_2, in_1, in_1);
endmodule

module myAND (
  input  in_1,
  input  in_2,
  output out_3
);

  wire nand_1_out;

  nand nand_1 (nand_1_out, in_1, in_2);
  myNOT mynot_1 (.in_1(nand_1_out), .out_2(out_3));
endmodule

module myOR (
  input  in_1,
  input  in_2,
  output out_3
);

  wire mynot_1_out_2, mynot_2_out_2;

  myNOT mynot_1 (.in_1(in_1), .out_2(mynot_1_out_2));
  myNOT mynot_2 (.in_1(in_2), .out_2(mynot_2_out_2));
  nand nand_1 (out_3, mynot_1_out_2, mynot_2_out_2);
endmodule

module myXOR (
  input  in_1,
  input  in_2,
  output out_3
);

  wire myand_1_out_3, myand_2_out_3, mynot_1_out_2, mynot_2_out_2;

  myNOT mynot_1 (.in_1(in_1), .out_2(mynot_1_out_2));
  myNOT mynot_2 (.in_1(in_2), .out_2(mynot_2_out_2));
  myAND myand_1 (.in_1(mynot_1_out_2), .in_2(in_2), .out_3(myand_1_out_3));
  myAND myand_2 (.in_1(in_1), .in_2(mynot_2_out_2), .out_3(myand_2_out_3));
  myOR myor_1 (.in_1(myand_1_out_3), .in_2(myand_2_out_3), .out_3(out_3));
endmodule

module myMUX (
  input  A,
  input  B,
  input  in_3,
  output out_4
);

  wire myand_1_out_3, myand_2_out_3, mynot_1_out_2;

  myNOT mynot_1 (.in_1(in_3), .out_2(mynot_1_out_2));
  myAND myand_1 (.in_1(A), .in_2(mynot_1_out_2), .out_3(myand_1_out_3));
  myAND myand_2 (.in_1(B), .in_2(in_3), .out_3(myand_2_out_3));
  myXOR myxor_1 (.in_1(myand_1_out_3), .in_2(myand_2_out_3), .out_3(out_4));
endmodule

module myDMUX (
  input  in_1,
  input  in_2,
  output out_3,
  output out_4
);

  wire mynot_1_out_2;

  myNOT mynot_1 (.in_1(in_2), .out_2(mynot_1_out_2));
  myAND myand_1 (.in_1(in_1), .in_2(mynot_1_out_2), .out_3(out_3));
  myAND myand_2 (.in_1(in_1), .in_2(in_2), .out_3(out_4));
endmodule

module myHalfAdder (
  input  in_1,
  input  in_2,
  output S,
  output C
);

  myXOR myxor_1 (.in_1(in_1), .in_2(in_2), .out_3(S));
  myAND myand_1 (.in_1(in_1), .in_2(in_2), .out_3(C));
endmodule

module myFullAdder (
  input  in_1,
  input  A,
  input  B,
  output S,
  output C
);

  wire myhalfadder_1_c, myhalfadder_1_s, myhalfadder_2_c;

  myHalfAdder myhalfadder_1 (.in_1(A), .in_2(B), .S(myhalfadder_1_s), .C(myhalfadder_1_c));
  myHalfAdder myhalfadder_2 (.in_1(in_1), .in_2(myhalfadder_1_s), .S(S), .C(myhalfadder_2_c));
  myOR myor_1 (.in_1(myhalfadder_2_c), .in_2(myhalfadder_1_c), .out_3(C));
endmodule

module myALU (
  input  A,
  input  B,
  input  C,
  input  L,
  input  R,
  input  S3,
  input  S2,
  input  S1,
  input  S0,
  output out_10,
  output Cout
);

  wire myand_1_out_3, myand_2_out_3, myand_3_out_3, myau_1_s, mylu_1_out_7, mymux_1_out_4, mynot_1_out_2,
       myor_1_out_3, myor_2_out_3, mysu_1_out_4, myxor_1_out_3;

  myAU myau_1 (.Cin(C), .A(A), .B(B), .S3(S3), .S2(S2), .S1(S1), .S0(S0), .S(myau_1_s), .Cout(Cout));
  myLU mylu_1 (.A(A), .B(B), .S3(S3), .S2(S2), .S1(S1), .S0(S0), .out_7(mylu_1_out_7));
  mySU mysu_1 (.R(L), .L(R), .S0(S1), .out_4(mysu_1_out_4));
  myOR myor_1 (.in_1(S3), .in_2(myand_1_out_3), .out_3(myor_1_out_3));
  myAND myand_1 (.in_1(S2), .in_2(myor_2_out_3), .out_3(myand_1_out_3));
  myOR myor_2 (.in_1(S1), .in_2(S0), .out_3(myor_2_out_3));
  myMUX mymux_1 (.A(myau_1_s), .B(mylu_1_out_7), .in_3(myor_1_out_3), .out_4(mymux_1_out_4));
  myAND myand_2 (.in_1(myxor_1_out_3), .in_2(myand_3_out_3), .out_3(myand_2_out_3));
  myXOR myxor_1 (.in_1(S1), .in_2(S0), .out_3(myxor_1_out_3));
  myAND myand_3 (.in_1(S3), .in_2(mynot_1_out_2), .out_3(myand_3_out_3));
  myNOT mynot_1 (.in_1(S2), .out_2(mynot_1_out_2));
  myMUX mymux_2 (.A(mymux_1_out_4), .B(mysu_1_out_4), .in_3(myand_2_out_3), .out_4(out_10));
endmodule

module myLU (
  input  A,
  input  B,
  input  S3,
  input  S2,
  input  S1,
  input  S0,
  output out_7
);

  wire myand_1_out_3, myand_2_out_3, myand_3_out_3, myand_4_out_3, myand_5_out_3, myand_6_out_3,
       myand_7_out_3, myand_8_out_3, myand_9_out_3, myand_10_out_3, myand_11_out_3, myand_12_out_3,
       mymux_1_out_4, mymux_2_out_4, mymux_3_out_4, mymux_4_out_4, mynot_1_out_2, mynot_2_out_2,
       mynot_3_out_2, mynot_4_out_2, mynot_5_out_2, mynot_6_out_2, myor_1_out_3, myor_2_out_3, myor_3_out_3,
       myor_4_out_3, myor_5_out_3, myor_6_out_3, myor_7_out_3, myxor_1_out_3;

  myAND myand_1 (.in_1(A), .in_2(B), .out_3(myand_1_out_3));
  myOR myor_1 (.in_1(A), .in_2(B), .out_3(myor_1_out_3));
  myXOR myxor_1 (.in_1(A), .in_2(B), .out_3(myxor_1_out_3));
  myNOT mynot_1 (.in_1(A), .out_2(mynot_1_out_2));
  myOR myor_2 (.in_1(myand_2_out_3), .in_2(myand_8_out_3), .out_3(myor_2_out_3));
  myAND myand_2 (.in_1(myand_3_out_3), .in_2(myand_5_out_3), .out_3(myand_2_out_3));
  myAND myand_3 (.in_1(S3), .in_2(mynot_2_out_2), .out_3(myand_3_out_3));
  myNOT mynot_2 (.in_1(S2), .out_2(mynot_2_out_2));
  myOR myor_3 (.in_1(myor_2_out_3), .in_2(myand_4_out_3), .out_3(myor_3_out_3));
  myAND myand_4 (.in_1(myand_12_out_3), .in_2(myand_7_out_3), .out_3(myand_4_out_3));
  myAND myand_5 (.in_1(mynot_3_out_2), .in_2(mynot_4_out_2), .out_3(myand_5_out_3));
  myNOT mynot_3 (.in_1(S1), .out_2(mynot_3_out_2));
  myNOT mynot_4 (.in_1(S0), .out_2(mynot_4_out_2));
  myMUX mymux_1 (.A(myand_1_out_3), .B(myor_1_out_3), .in_3(myor_3_out_3), .out_4(mymux_1_out_4));
  myOR myor_4 (.in_1(myor_5_out_3), .in_2(myor_6_out_3), .out_3(myor_4_out_3));
  myMUX mymux_2 (.A(myxor_1_out_3), .B(mynot_1_out_2), .in_3(myor_3_out_3), .out_4(mymux_2_out_4));
  myMUX mymux_3 (.A(A), .B(B), .in_3(myor_3_out_3), .out_4(mymux_3_out_4));
  myOR myor_5 (.in_1(myand_11_out_3), .in_2(myand_6_out_3), .out_3(myor_5_out_3));
  myOR myor_6 (.in_1(myand_2_out_3), .in_2(myand_8_out_3), .out_3(myor_6_out_3));
  myAND myand_6 (.in_1(myand_7_out_3), .in_2(myand_9_out_3), .out_3(myand_6_out_3));
  myAND myand_7 (.in_1(S1), .in_2(mynot_5_out_2), .out_3(myand_7_out_3));
  myNOT mynot_5 (.in_1(S0), .out_2(mynot_5_out_2));
  myAND myand_8 (.in_1(myand_9_out_3), .in_2(myand_10_out_3), .out_3(myand_8_out_3));
  myAND myand_9 (.in_1(S3), .in_2(S2), .out_3(myand_9_out_3));
  myAND myand_10 (.in_1(S1), .in_2(S0), .out_3(myand_10_out_3));
  myMUX mymux_4 (.A(mymux_1_out_4), .B(mymux_2_out_4), .in_3(myor_4_out_3), .out_4(mymux_4_out_4));
  myOR myor_7 (.in_1(myand_6_out_3), .in_2(myand_8_out_3), .out_3(myor_7_out_3));
  myAND myand_11 (.in_1(myand_10_out_3), .in_2(myand_12_out_3), .out_3(myand_11_out_3));
  myAND myand_12 (.in_1(S2), .in_2(mynot_6_out_2), .out_3(myand_12_out_3));
  myNOT mynot_6 (.in_1(S3), .out_2(mynot_6_out_2));
  myMUX mymux_5 (.A(mymux_4_out_4), .B(mymux_3_out_4), .in_3(myor_7_out_3), .out_4(out_7));
endmodule

module myAU (
  input  Cin,
  input  A,
  input  B,
  input  S3,
  input  S2,
  input  S1,
  input  S0,
  output S,
  output Cout
);

  wire myand_1_out_3, myand_2_out_3, myand_3_out_3, myand_4_out_3, myand_5_out_3, myand_6_out_3,
       myand_7_out_3, myand_8_out_3, myand_9_out_3, myand_10_out_3, mynot_1_out_2, mynot_2_out_2,
       mynot_3_out_2, mynot_4_out_2, mynot_5_out_2, mynot_6_out_2, mynot_7_out_2, myor_1_out_3, myor_2_out_3,
       myor_3_out_3, myor_4_out_3, myor_5_out_3, myor_6_out_3, myxor_1_out_3, myxor_2_out_3;

  myOR myor_1 (.in_1(B), .in_2(myand_1_out_3), .out_3(myor_1_out_3));
  myAND myand_1 (.in_1(myand_2_out_3), .in_2(myand_7_out_3), .out_3(myand_1_out_3));
  myAND myand_2 (.in_1(S1), .in_2(S0), .out_3(myand_2_out_3));
  myAND myand_3 (.in_1(myand_4_out_3), .in_2(myand_5_out_3), .out_3(myand_3_out_3));
  myAND myand_4 (.in_1(S2), .in_2(mynot_1_out_2), .out_3(myand_4_out_3));
  myAND myand_5 (.in_1(mynot_2_out_2), .in_2(mynot_3_out_2), .out_3(myand_5_out_3));
  myNOT mynot_1 (.in_1(S3), .out_2(mynot_1_out_2));
  myNOT mynot_2 (.in_1(S1), .out_2(mynot_2_out_2));
  myNOT mynot_3 (.in_1(S0), .out_2(mynot_3_out_2));
  myOR myor_2 (.in_1(myor_1_out_3), .in_2(myand_3_out_3), .out_3(myor_2_out_3));
  myOR myor_3 (.in_1(myand_3_out_3), .in_2(myand_6_out_3), .out_3(myor_3_out_3));
  myAND myand_6 (.in_1(myand_7_out_3), .in_2(myand_8_out_3), .out_3(myand_6_out_3));
  myAND myand_7 (.in_1(mynot_4_out_2), .in_2(mynot_5_out_2), .out_3(myand_7_out_3));
  myNOT mynot_4 (.in_1(S3), .out_2(mynot_4_out_2));
  myOR myor_4 (.in_1(myand_3_out_3), .in_2(myor_5_out_3), .out_3(myor_4_out_3));
  myOR myor_5 (.in_1(myand_6_out_3), .in_2(myand_9_out_3), .out_3(myor_5_out_3));
  myAND myand_8 (.in_1(mynot_6_out_2), .in_2(S0), .out_3(myand_8_out_3));
  myNOT mynot_5 (.in_1(S2), .out_2(mynot_5_out_2));
  myNOT mynot_6 (.in_1(S1), .out_2(mynot_6_out_2));
  myAND myand_9 (.in_1(myand_7_out_3), .in_2(myand_10_out_3), .out_3(myand_9_out_3));
  myAND myand_10 (.in_1(S1), .in_2(mynot_7_out_2), .out_3(myand_10_out_3));
  myNOT mynot_7 (.in_1(S0), .out_2(mynot_7_out_2));
  myOR myor_6 (.in_1(Cin), .in_2(myor_4_out_3), .out_3(myor_6_out_3));
  myXOR myxor_1 (.in_1(A), .in_2(myand_9_out_3), .out_3(myxor_1_out_3));
  myXOR myxor_2 (.in_1(myor_2_out_3), .in_2(myor_3_out_3), .out_3(myxor_2_out_3));
  myFullAdder myfulladder_1 (.in_1(myor_6_out_3), .A(myxor_1_out_3), .B(myxor_2_out_3), .S(S), .C(Cout));
endmodule

module mySU (
  input  R,
  input  L,
  input  S0,
  output out_4
);

  myMUX mymux_1 (.A(R), .B(L), .in_3(S0), .out_4(out_4));
endmodule

module my8bitALU (
  input  [7:0] A,
  input  [7:0] B,
  input  [3:0] in_3,
  output [7:0] out_4,
  output Carry
);

  wire myand_1_out_3, myand_2_out_3, myand_3_out_3, myand_4_out_3, myand_5_out_3, myand_6_out_3,
       myand_7_out_3, myand_8_out_3, mynot_1_out_2, mynot_2_out_2, mynot_3_out_2, myor_1_out_3, myor_2_out_3,
       myor_3_out_3, myor_4_out_3, myxor_1_out_3;
  wire [7:0] my8bitau_1_out_6, my8bitcmp_1_out_4, my8bitlu_1_out_4, my8bitmux_1_out_4, my8bitmux_2_out_4,
       my8bitsu_1_out_3;

  my8bitAU my8bitau_1 (.A(A), .B(B), .S2(in_3[2]), .S1(in_3[1]), .S0(in_3[0]), .out_6(my8bitau_1_out_6), .Cout(Carry));
  my8bitLU my8bitlu_1 (.A(A), .B(B), .in_3(in_3), .out_4(my8bitlu_1_out_4));
  my8bitSU my8bitsu_1 (.in_1(A), .in_2(in_3[1]), .out_3(my8bitsu_1_out_3));
  my8bitCMP my8bitcmp_1 (.A(A), .B(B), .out_4(my8bitcmp_1_out_4));  // open: in_3
  myAND myand_1 (.in_1(myand_2_out_3), .in_2(in_3[3]), .out_3(myand_1_out_3));
  myAND myand_2 (.in_1(in_3[0]), .in_2(in_3[1]), .out_3(myand_2_out_3));
  myOR myor_1 (.in_1(myor_2_out_3), .in_2(myor_3_out_3), .out_3(myor_1_out_3));
  myOR myor_2 (.in_1(myand_1_out_3), .in_2(myand_3_out_3), .out_3(myor_2_out_3));
  myAND myand_3 (.in_1(in_3[0]), .in_2(in_3[2]), .out_3(myand_3_out_3));
  myOR myor_3 (.in_1(myand_4_out_3), .in_2(myand_5_out_3), .out_3(myor_3_out_3));
  myAND myand_4 (.in_1(in_3[1]), .in_2(in_3[2]), .out_3(myand_4_out_3));
  myAND myand_5 (.in_1(in_3[3]), .in_2(myand_6_out_3), .out_3(myand_5_out_3));
  myAND myand_6 (.in_1(mynot_2_out_2), .in_2(mynot_1_out_2), .out_3(myand_6_out_3));
  myNOT mynot_1 (.in_1(in_3[0]), .out_2(mynot_1_out_2));
  myNOT mynot_2 (.in_1(in_3[1]), .out_2(mynot_2_out_2));
  my8bitMUX my8bitmux_1 (
    .in_1(my8bitau_1_out_6), .in_2(my8bitlu_1_out_4), .in_3(myor_1_out_3), .out_4(my8bitmux_1_out_4));
  my8bitMUX my8bitmux_2 (
    .in_1(my8bitsu_1_out_3), .in_2(my8bitcmp_1_out_4), .in_3(myor_1_out_3), .out_4(my8bitmux_2_out_4));
  myXOR myxor_1 (.in_1(in_3[1]), .in_2(in_3[2]), .out_3(myxor_1_out_3));
  myAND myand_7 (.in_1(in_3[3]), .in_2(myor_4_out_3), .out_3(myand_7_out_3));
  myOR myor_4 (.in_1(myxor_1_out_3), .in_2(myand_8_out_3), .out_3(myor_4_out_3));
  myAND myand_8 (.in_1(in_3[0]), .in_2(mynot_3_out_2), .out_3(myand_8_out_3));
  myNOT mynot_3 (.in_1(in_3[2]), .out_2(mynot_3_out_2));
  my8bitMUX my8bitmux_3 (.in_1(my8bitmux_1_out_4), .in_2(my8bitmux_2_out_4), .in_3(myand_7_out_3), .out_4(out_4));
endmodule

module my8bitAU (
  input  [7:0] A,
  input  [7:0] B,
  input  S2,
  input  S1,
  input  S0,
  output [7:0] out_6,
  output Cout
);

  wire myand_1_out_3, myand_2_out_3, myand_3_out_3, myand_4_out_3, myand_5_out_3, myand_6_out_3,
       myand_7_out_3, myand_8_out_3, myfulladder_1_c, myfulladder_2_c, myfulladder_3_c, myfulladder_4_c,
       myfulladder_5_c, myfulladder_6_c, myfulladder_7_c, mynot_1_out_2, mynot_2_out_2, mynot_3_out_2,
       mynot_4_out_2, mynot_5_out_2, myor_1_out_3, myor_2_out_3, myor_3_out_3, myor_4_out_3, myor_5_out_3,
       myxor_1_out_3, myxor_2_out_3, myxor_3_out_3, myxor_4_out_3, myxor_5_out_3, myxor_6_out_3,
       myxor_7_out_3, myxor_8_out_3, myxor_9_out_3, myxor_10_out_3, myxor_11_out_3, myxor_12_out_3,
       myxor_13_out_3, myxor_14_out_3, myxor_15_out_3, myxor_16_out_3;

  myOR myor_1 (.in_1(myand_1_out_3), .in_2(myand_3_out_3), .out_3(myor_1_out_3));
  myAND myand_1 (.in_1(myand_2_out_3), .in_2(mynot_4_out_2), .out_3(myand_1_out_3));
  myAND myand_2 (.in_1(S1), .in_2(S0), .out_3(myand_2_out_3));
  myAND myand_3 (.in_1(S2), .in_2(myand_4_out_3), .out_3(myand_3_out_3));
  myAND myand_4 (.in_1(mynot_1_out_2), .in_2(mynot_2_out_2), .out_3(myand_4_out_3));
  myNOT mynot_1 (.in_1(S1), .out_2(mynot_1_out_2));
  myNOT mynot_2 (.in_1(S0), .out_2(mynot_2_out_2));
  myOR myor_2 (.in_1(B[0]), .in_2(myor_1_out_3), .out_3(myor_2_out_3));
  myOR myor_3 (.in_1(myand_3_out_3), .in_2(myand_7_out_3), .out_3(myor_3_out_3));
  myAND myand_5 (.in_1(mynot_4_out_2), .in_2(myand_6_out_3), .out_3(myand_5_out_3));
  myAND myand_6 (.in_1(S1), .in_2(mynot_3_out_2), .out_3(myand_6_out_3));
  myNOT mynot_3 (.in_1(S0), .out_2(mynot_3_out_2));
  myOR myor_4 (.in_1(myand_3_out_3), .in_2(myor_5_out_3), .out_3(myor_4_out_3));
  myOR myor_5 (.in_1(myand_7_out_3), .in_2(myand_5_out_3), .out_3(myor_5_out_3));
  myAND myand_7 (.in_1(mynot_4_out_2), .in_2(myand_8_out_3), .out_3(myand_7_out_3));
  myAND myand_8 (.in_1(mynot_5_out_2), .in_2(S0), .out_3(myand_8_out_3));
  myNOT mynot_4 (.in_1(S2), .out_2(mynot_4_out_2));
  myNOT mynot_5 (.in_1(S1), .out_2(mynot_5_out_2));
  myXOR myxor_1 (.in_1(A[0]), .in_2(myand_5_out_3), .out_3(myxor_1_out_3));
  myXOR myxor_2 (.in_1(myor_2_out_3), .in_2(myor_3_out_3), .out_3(myxor_2_out_3));
  myXOR myxor_3 (.in_1(A[1]), .in_2(myand_5_out_3), .out_3(myxor_3_out_3));
  myXOR myxor_4 (.in_1(B[1]), .in_2(myor_3_out_3), .out_3(myxor_4_out_3));
  myXOR myxor_5 (.in_1(A[2]), .in_2(myand_5_out_3), .out_3(myxor_5_out_3));
  myXOR myxor_6 (.in_1(B[2]), .in_2(myor_3_out_3), .out_3(myxor_6_out_3));
  myXOR myxor_7 (.in_1(A[3]), .in_2(myand_5_out_3), .out_3(myxor_7_out_3));
  myXOR myxor_8 (.in_1(B[3]), .in_2(myor_3_out_3), .out_3(myxor_8_out_3));
  myXOR myxor_9 (.in_1(A[4]), .in_2(myand_5_out_3), .out_3(myxor_9_out_3));
  myXOR myxor_10 (.in_1(B[4]), .in_2(myor_3_out_3), .out_3(myxor_10_out_3));
  myXOR myxor_11 (.in_1(A[5]), .in_2(myand_5_out_3), .out_3(myxor_11_out_3));
  myXOR myxor_12 (.in_1(B[5]), .in_2(myor_3_out_3), .out_3(myxor_12_out_3));
  myXOR myxor_13 (.in_1(A[6]), .in_2(myand_5_out_3), .out_3(myxor_13_out_3));
  myXOR myxor_14 (.in_1(B[6]), .in_2(myor_3_out_3), .out_3(myxor_14_out_3));
  myXOR myxor_15 (.in_1(A[7]), .in_2(myand_5_out_3), .out_3(myxor_15_out_3));
  myXOR myxor_16 (.in_1(B[7]), .in_2(myor_3_out_3), .out_3(myxor_16_out_3));
  myFullAdder myfulladder_1 (
    .in_1(myor_4_out_3), .A(myxor_1_out_3), .B(myxor_2_out_3), .S(out_6[0]), .C(myfulladder_1_c));
  myFullAdder myfulladder_2 (
    .in_1(myfulladder_1_c), .A(myxor_3_out_3), .B(myxor_4_out_3), .S(out_6[1]), .C(myfulladder_2_c));
  myFullAdder myfulladder_3 (
    .in_1(myfulladder_2_c), .A(myxor_5_out_3), .B(myxor_6_out_3), .S(out_6[2]), .C(myfulladder_3_c));
  myFullAdder myfulladder_4 (
    .in_1(myfulladder_3_c), .A(myxor_7_out_3), .B(myxor_8_out_3), .S(out_6[3]), .C(myfulladder_4_c));
  myFullAdder myfulladder_5 (
    .in_1(myfulladder_4_c), .A(myxor_9_out_3), .B(myxor_10_out_3), .S(out_6[4]), .C(myfulladder_5_c));
  myFullAdder myfulladder_6 (
    .in_1(myfulladder_5_c), .A(myxor_11_out_3), .B(myxor_12_out_3), .S(out_6[5]), .C(myfulladder_6_c));
  myFullAdder myfulladder_7 (
    .in_1(myfulladder_6_c), .A(myxor_13_out_3), .B(myxor_14_out_3), .S(out_6[6]), .C(myfulladder_7_c));
  myFullAdder myfulladder_8 (.in_1(myfulladder_7_c), .A(myxor_15_out_3), .B(myxor_16_out_3), .S(out_6[7]), .C(Cout));
endmodule

module my8bitLU (
  input  [7:0] A,
  input  [7:0] B,
  input  [3:0] in_3,
  output [7:0] out_4
);

  myLU mylu_1 (.A(A[0]), .B(B[0]), .S3(in_3[3]), .S2(in_3[2]), .S1(in_3[1]), .S0(in_3[0]), .out_7(out_4[0]));
  myLU mylu_2 (.A(A[1]), .B(B[1]), .S3(in_3[3]), .S2(in_3[2]), .S1(in_3[1]), .S0(in_3[0]), .out_7(out_4[1]));
  myLU mylu_3 (.A(A[2]), .B(B[2]), .S3(in_3[3]), .S2(in_3[2]), .S1(in_3[1]), .S0(in_3[0]), .out_7(out_4[2]));
  myLU mylu_4 (.A(A[3]), .B(B[3]), .S3(in_3[3]), .S2(in_3[2]), .S1(in_3[1]), .S0(in_3[0]), .out_7(out_4[3]));
  myLU mylu_5 (.A(A[4]), .B(B[4]), .S3(in_3[3]), .S2(in_3[2]), .S1(in_3[1]), .S0(in_3[0]), .out_7(out_4[4]));
  myLU mylu_6 (.A(A[5]), .B(B[5]), .S3(in_3[3]), .S2(in_3[2]), .S1(in_3[1]), .S0(in_3[0]), .out_7(out_4[5]));
  myLU mylu_7 (.A(A[6]), .B(B[6]), .S3(in_3[3]), .S2(in_3[2]), .S1(in_3[1]), .S0(in_3[0]), .out_7(out_4[6]));
  myLU mylu_8 (.A(A[7]), .B(B[7]), .S3(in_3[3]), .S2(in_3[2]), .S1(in_3[1]), .S0(in_3[0]), .out_7(out_4[7]));
endmodule

module my8bitSU (
  input  [7:0] in_1,
  input  in_2,
  output [7:0] out_3
);

  mySU mysu_1 (.L(in_1[1]), .S0(in_2), .out_4(out_3[0]));  // open: R
  mySU mysu_2 (.R(in_1[0]), .L(in_1[2]), .S0(in_2), .out_4(out_3[1]));
  mySU mysu_3 (.R(in_1[1]), .L(in_1[3]), .S0(in_2), .out_4(out_3[2]));
  mySU mysu_4 (.R(in_1[2]), .L(in_1[4]), .S0(in_2), .out_4(out_3[3]));
  mySU mysu_5 (.R(in_1[3]), .L(in_1[5]), .S0(in_2), .out_4(out_3[4]));
  mySU mysu_6 (.R(in_1[4]), .L(in_1[6]), .S0(in_2), .out_4(out_3[5]));
  mySU mysu_7 (.R(in_1[5]), .L(in_1[7]), .S0(in_2), .out_4(out_3[6]));
  mySU mysu_8 (.R(in_1[6]), .S0(in_2), .out_4(out_3[7]));  // open: L
endmodule

module my8bitMUX (
  input  [7:0] in_1,
  input  [7:0] in_2,
  input  in_3,
  output [7:0] out_4
);

  myMUX mymux_1 (.A(in_1[0]), .B(in_2[0]), .in_3(in_3), .out_4(out_4[0]));
  myMUX mymux_2 (.A(in_1[1]), .B(in_2[1]), .in_3(in_3), .out_4(out_4[1]));
  myMUX mymux_3 (.A(in_1[2]), .B(in_2[2]), .in_3(in_3), .out_4(out_4[2]));
  myMUX mymux_4 (.A(in_1[3]), .B(in_2[3]), .in_3(in_3), .out_4(out_4[3]));
  myMUX mymux_5 (.A(in_1[4]), .B(in_2[4]), .in_3(in_3), .out_4(out_4[4]));
  myMUX mymux_6 (.A(in_1[5]), .B(in_2[5]), .in_3(in_3), .out_4(out_4[5]));
  myMUX mymux_7 (.A(in_1[6]), .B(in_2[6]), .in_3(in_3), .out_4(out_4[6]));
  myMUX mymux_8 (.A(in_1[7]), .B(in_2[7]), .in_3(in_3), .out_4(out_4[7]));
endmodule

module my8bitCMP (
  input  [7:0] A,
  input  [7:0] B,
  input  [1:0] in_3,
  output [7:0] out_4
);

  wire myand_1_out_3, myand_2_out_3, mycmp_1_ctout, mycmp_1_eqout, mycmp_2_ctout, mycmp_2_eqout,
       mycmp_3_ctout, mycmp_3_eqout, mycmp_4_ctout, mycmp_4_eqout, mycmp_5_ctout, mycmp_5_eqout,
       mycmp_6_ctout, mycmp_6_eqout, mycmp_7_ctout, mycmp_7_eqout, mycmp_8_ctout, mycmp_8_eqout,
       mymux_1_out_4, mynot_1_out_2, mynot_2_out_2, mynot_3_out_2;

  myCMP mycmp_1 (.A(B[0]), .B(A[0]), .EQout(mycmp_1_eqout), .CTout(mycmp_1_ctout));  // open: EQin, CTin
  myCMP mycmp_2 (
    .EQin(mycmp_1_eqout), .A(B[1]), .B(A[1]), .CTin(mycmp_1_ctout), .EQout(mycmp_2_eqout),
    .CTout(mycmp_2_ctout));
  myCMP mycmp_3 (
    .EQin(mycmp_2_eqout), .A(B[2]), .B(A[2]), .CTin(mycmp_2_ctout), .EQout(mycmp_3_eqout),
    .CTout(mycmp_3_ctout));
  myCMP mycmp_4 (
    .EQin(mycmp_3_eqout), .A(B[3]), .B(A[3]), .CTin(mycmp_3_ctout), .EQout(mycmp_4_eqout),
    .CTout(mycmp_4_ctout));
  myCMP mycmp_5 (
    .EQin(mycmp_4_eqout), .A(B[4]), .B(A[4]), .CTin(mycmp_4_ctout), .EQout(mycmp_5_eqout),
    .CTout(mycmp_5_ctout));
  myCMP mycmp_6 (
    .EQin(mycmp_5_eqout), .A(B[5]), .B(A[5]), .CTin(mycmp_5_ctout), .EQout(mycmp_6_eqout),
    .CTout(mycmp_6_ctout));
  myCMP mycmp_7 (
    .EQin(mycmp_6_eqout), .A(B[6]), .B(A[6]), .CTin(mycmp_6_ctout), .EQout(mycmp_7_eqout),
    .CTout(mycmp_7_ctout));
  myCMP mycmp_8 (
    .EQin(mycmp_7_eqout), .A(B[7]), .B(A[7]), .CTin(mycmp_7_ctout), .EQout(mycmp_8_eqout),
    .CTout(mycmp_8_ctout));
  myNOT mynot_1 (.in_1(mycmp_8_ctout), .out_2(mynot_1_out_2));
  myNOT mynot_2 (.in_1(mycmp_8_eqout), .out_2(mynot_2_out_2));
  myAND myand_1 (.in_1(mynot_1_out_2), .in_2(mynot_2_out_2), .out_3(myand_1_out_3));
  myNOT mynot_3 (.in_1(in_3[1]), .out_2(mynot_3_out_2));
  myMUX mymux_1 (.A(mycmp_8_eqout), .B(mycmp_8_ctout), .in_3(mynot_3_out_2), .out_4(mymux_1_out_4));
  myAND myand_2 (.in_1(mynot_3_out_2), .in_2(in_3[0]), .out_3(myand_2_out_3));
  myMUX mymux_2 (.A(mymux_1_out_4), .B(myand_1_out_3), .in_3(myand_2_out_3), .out_4(out_4[7]));

  assign out_4[6:0] = {7{out_4[7]}};
endmodule

module myCMP (
  input  EQin,
  input  A,
  input  B,
  input  CTin,
  output EQout,
  output CTout
);

  wire myand_1_out_3, myand_3_out_3, myand_4_out_3, mynot_1_out_2, mynot_2_out_2, myxor_1_out_3;

  myXOR myxor_1 (.in_1(A), .in_2(B), .out_3(myxor_1_out_3));
  myNOT mynot_1 (.in_1(B), .out_2(mynot_1_out_2));
  myNOT mynot_2 (.in_1(myxor_1_out_3), .out_2(mynot_2_out_2));
  myAND myand_1 (.in_1(A), .in_2(mynot_1_out_2), .out_3(myand_1_out_3));
  myAND myand_2 (.in_1(EQin), .in_2(mynot_2_out_2), .out_3(EQout));
  myAND myand_3 (.in_1(myand_1_out_3), .in_2(EQin), .out_3(myand_3_out_3));
  myAND myand_4 (.in_1(mynot_2_out_2), .in_2(CTin), .out_3(myand_4_out_3));
  myOR myor_1 (.in_1(myand_4_out_3), .in_2(myand_3_out_3), .out_3(CTout));
endmodule

module myRegister (
  input  [7:0] D,
  input  CLK,
  output [7:0] out_3
);

  D_Flip_Flop d_ff_1 (.D(D[0]), .clk(CLK), .Q(out_3[0]), .Qn(out_3[1]));  // open: preset, reset
  D_Flip_Flop d_ff_2 (.D(D[1]), .clk(CLK), .Q(out_3[1]));  // open: Qn, preset, reset
  D_Flip_Flop d_ff_3 (.D(D[2]), .clk(CLK), .Q(out_3[2]));  // open: Qn, preset, reset
  D_Flip_Flop d_ff_4 (.D(D[3]), .clk(CLK), .Q(out_3[3]));  // open: Qn, preset, reset
  D_Flip_Flop d_ff_5 (.D(D[4]), .clk(CLK), .Q(out_3[4]));  // open: Qn, preset, reset
  D_Flip_Flop d_ff_6 (.D(D[5]), .clk(CLK), .Q(out_3[5]));  // open: Qn, preset, reset
  D_Flip_Flop d_ff_7 (.D(D[6]), .clk(CLK), .Q(out_3[6]));  // open: Qn, preset, reset
  D_Flip_Flop d_ff_8 (.D(D[7]), .clk(CLK), .Q(out_3[7]));  // open: Qn, preset, reset
endmodule

module myProgramCounter (
  input  [7:0] One,
  input  CLK,
  input  [7:0] Zero,
  input  Reset,
  input  [7:0] JumpAdress,
  input  Load,
  output [7:0] Q
);

  wire [7:0] my8bitau_1_out_6, my8bitmux_1_out_4, my8bitmux_2_out_4;

  Register register_1 (.D(my8bitau_1_out_6), .clk(CLK), .Q(Q), .clr(Reset));  // open: en
  my8bitMUX my8bitmux_1 (.in_1(Q), .in_2(JumpAdress), .in_3(Load), .out_4(my8bitmux_1_out_4));
  my8bitMUX my8bitmux_2 (.in_1(One), .in_2(Zero), .in_3(Load), .out_4(my8bitmux_2_out_4));
  my8bitAU my8bitau_1 (
    .A(my8bitmux_1_out_4), .B(my8bitmux_2_out_4), .out_6(my8bitau_1_out_6));  // open: S2, S1, S0, Cout
endmodule

module myControlUnit (
  input  [7:0] RAM,
  output [3:0] opocode,
  output loadA,
  output loadD,
  output aluBMux,
  output writeM,
  output jumpEnable
);

  wire myand_1_out_3, myand_2_out_3, myand_3_out_3, myand_4_out_3, myand_5_out_3, myand_6_out_3,
       myand_7_out_3, myand_8_out_3, myand_9_out_3, myand_10_out_3, myand_11_out_3, mynot_1_out_2,
       mynot_2_out_2, mynot_3_out_2, myor_1_out_3, myor_2_out_3, myor_3_out_3;

  myNOT mynot_1 (.in_1(RAM[2]), .out_2(mynot_1_out_2));
  myNOT mynot_2 (.in_1(RAM[1]), .out_2(mynot_2_out_2));
  myNOT mynot_3 (.in_1(RAM[0]), .out_2(mynot_3_out_2));
  myAND myand_1 (.in_1(mynot_2_out_2), .in_2(mynot_3_out_2), .out_3(myand_1_out_3));
  myAND myand_2 (.in_1(mynot_2_out_2), .in_2(RAM[0]), .out_3(myand_2_out_3));
  myAND myand_3 (.in_1(RAM[1]), .in_2(mynot_3_out_2), .out_3(myand_3_out_3));
  myAND myand_4 (.in_1(RAM[1]), .in_2(RAM[0]), .out_3(myand_4_out_3));
  myAND myand_5 (.in_1(mynot_1_out_2), .in_2(myand_1_out_3), .out_3(myand_5_out_3));
  myAND myand_6 (.in_1(mynot_1_out_2), .in_2(myand_2_out_3), .out_3(myand_6_out_3));
  myAND myand_7 (.in_1(mynot_1_out_2), .in_2(myand_3_out_3), .out_3(myand_7_out_3));
  myAND myand_8 (.in_1(mynot_1_out_2), .in_2(myand_4_out_3), .out_3(myand_8_out_3));
  myAND myand_9 (.in_1(RAM[2]), .in_2(myand_1_out_3), .out_3(myand_9_out_3));
  myAND myand_10 (.in_1(RAM[2]), .in_2(myand_2_out_3), .out_3(myand_10_out_3));
  myAND myand_11 (.in_1(RAM[2]), .in_2(myand_3_out_3), .out_3(myand_11_out_3));
  myAND myand_12 (.in_1(RAM[2]), .in_2(myand_4_out_3), .out_3(myand_6_out_3));
  myOR myor_1 (.in_1(myand_7_out_3), .in_2(myand_6_out_3), .out_3(myor_1_out_3));
  myOR myor_2 (.in_1(myand_6_out_3), .in_2(myand_6_out_3), .out_3(myor_2_out_3));
  myOR myor_3 (.in_1(myand_9_out_3), .in_2(myand_11_out_3), .out_3(myor_3_out_3));
  myOR myor_4 (.in_1(myand_8_out_3), .in_2(myand_9_out_3), .out_3(writeM));
  myOR myor_5 (.in_1(myand_10_out_3), .in_2(myand_11_out_3), .out_3(jumpEnable));
  myOR myor_6 (.in_1(RAM[7]), .in_2(myor_1_out_3), .out_3(loadA));
  myOR myor_7 (.in_1(myand_5_out_3), .in_2(myor_2_out_3), .out_3(loadD));
  myOR myor_8 (.in_1(myand_6_out_3), .in_2(myor_3_out_3), .out_3(aluBMux));

  assign opocode = RAM[6:3];
endmodule
